# Fritzing sketch Push_or_reed (saved by Fritzing 0.9.3b)
breadboards: 1

parts:
  Part1 = Arduino Uno (Rev3)
  R1 = Resistor [tolerance=±5% resistance=100 package=THT]
  S1 = Pushbutton [package="[THT]"]
  LED1 = LED - 5mm [color="Red (633nm)" package="5 mm [THT]"]

nets:
  N1: Part1.D13/SCK, LED1.anode
  N2: Part1.D3_PWM, S1.Pin_1, S1.Pin_2
  N3: Part1.3V3, R1.Pin_0
  N4: Part1.GND, LED1.cathode
  N5: R1.Pin_1, S1.Pin_3, S1.Pin_4

// code stored in the sketch: Push_or_Reed_button.ino
#define BUTTON_PIN 3
void setup() {

  pinMode(BUTTON_PIN, INPUT);
  digitalWrite (BUTTON_PIN, LOW);

  pinMode(13, OUTPUT);
  digitalWrite (13, LOW);


  Serial.begin(115200);
  Serial.println(F("RF24/examples/GettingStarted"));
}
bool  val ;
void loop() {
  if (digitalRead(BUTTON_PIN) == 0)
  {
    Serial.println("closed");
    digitalWrite (13, HIGH);
  }
  else
  {
    Serial.println("Open");
    digitalWrite (13, LOW);
  }
  delay(500);
}
